// Logisim project CPU_logisim.circ as structural Verilog: 7 circuits, main circuit main
module main (
  input  Reset,
  output [31:0] out_2,
  output out_3,
  output [4:0] out_4,
  output [31:0] out_5,
  output out_6,
  output [4:0] out_7,
  output [31:0] out_8
);

  wire ALUSrc, clk, ExtOp, MemtoReg, nPC_sel, RegDst, zero;
  wire [3:0] ALUCtr;
  wire [31:0] busA, dm_1_mendata, MemAddr32, multiplexer_2_out, signImm;

  Clock clock_1 (.out(clk));
  IFU ifu_1 (.Zero(zero), .Br(nPC_sel), .Imm(signImm), .Do(out_2), .Reset(Reset), .Clk(clk));
  EXT ext_1 (.Imm16(out_2[15:0]), .ExtOp(ExtOp), .Imm32(signImm));
  Multiplexer #(.width(5), .enable("false")) multiplexer_1 (
    .in0(out_2[20:16]), .in1(out_2[15:11]), .out(out_4), .sel(RegDst));
  Multiplexer #(.width(32), .enable("false")) multiplexer_2 (
    .in0(out_8), .in1(signImm), .out(multiplexer_2_out), .sel(ALUSrc));
  Controller controller_1 (
    .func(out_2[5:0]), .OpCode(out_2[31:26]), .ALUCtr(ALUCtr), .RegDst(RegDst), .RegWrite(out_3),
    .MemtoReg(MemtoReg), .ALUSrc(ALUSrc), .MemWrite(out_6), .nPC_sel(nPC_sel), .ExtOp(ExtOp));
  GRF grf_1 (
    .RA(out_2[25:21]), .RB(out_2[20:16]), .RW(out_4), .WD(out_5), .busA(busA), .busB(out_8), .Clk(clk),
    .Reset(Reset), .WE(out_3));
  ALU alu_1 (
    .A(busA), .B(multiplexer_2_out), .ALUCtr(ALUCtr), .zero(zero),
    .Imm32({MemAddr32[31:7], out_7, MemAddr32[1:0]}));
  DM dm_1 (
    .Addr({MemAddr32[31:7], out_7, MemAddr32[1:0]}), .DataIn(out_8), .MenData(dm_1_mendata), .WrEn(out_6),
    .LdEn(1'b1), .Reset(Reset), .Clk(clk));
  Multiplexer #(.width(32), .enable("false")) multiplexer_3 (
    .in0({MemAddr32[31:7], out_7, MemAddr32[1:0]}), .in1(dm_1_mendata), .out(out_5), .sel(MemtoReg));

  // Other names for the same wires on the sheet: busB[31:0] = out_8; MemData[31:0] = out_8; func[5:0] = out_2[5:0];
  //   Imm[15:0] = out_2[15:0]; Instr[31:0] = out_2; rd[4:0] = out_2[15:11]; rt[4:0] = out_2[20:16];
  //   rs[4:0] = out_2[25:21]; OpCode[5:0] = out_2[31:26]; MemAddr[4:0] = out_7; MemAddr32[6:2] = out_7;
  //   MemWrite = out_6; RegAddr[4:0] = out_4; RegData[31:0] = out_5; RegWrite = out_3
endmodule

module GRF (
  input  Clk,
  input  Reset,
  input  WE,
  input  [4:0] RA,
  input  [4:0] RB,
  input  [4:0] RW,
  input  [31:0] WD,
  output [31:0] busA,
  output [31:0] busB
);

  wire and_1_out, and_2_out, and_3_out, and_4_out, and_5_out, and_6_out, and_7_out, and_8_out, and_9_out,
       and_10_out, and_11_out, and_12_out, and_13_out, and_14_out, and_15_out, and_16_out, and_17_out,
       and_18_out, and_19_out, and_20_out, and_21_out, and_22_out, and_23_out, and_24_out, and_25_out,
       and_26_out, and_27_out, and_28_out, and_29_out, and_30_out, and_31_out, d1, d2, d3, d4, d5, d6, d7,
       d8, d9, d10, d11, d12, d13, d14, d15, d16, d17, d18, d19, d20, d21, d22, d23, d24, d25, d26, d27, d28,
       d29, d30, d31;
  wire [31:0] o1, o2, o3, o4, o5, o6, o7, o8, o9, o10, o11, o12, o13, o14, o15, o16, o17, o18, o19, o20, o21,
       o22, o23, o24, o25, o26, o27, o28, o29, o30, o31;

  Decoder #(.select(5)) decoder_1 (
    .out1(d1), .out2(d2), .out3(d3), .out4(d4), .out5(d5), .out6(d6), .out7(d7), .out8(d8), .out9(d9),
    .out10(d10), .out11(d11), .out12(d12), .out13(d13), .out14(d14), .out15(d15), .out16(d16), .out17(d17),
    .out18(d18), .out19(d19), .out20(d20), .out21(d21), .out22(d22), .out23(d23), .out24(d24), .out25(d25),
    .out26(d26), .out27(d27), .out28(d28), .out29(d29), .out30(d30), .out31(d31), .sel(RW));  // open: out0, en
  and and_1 (and_1_out, WE, d1);
  and and_2 (and_2_out, WE, d2);
  and and_3 (and_3_out, WE, d3);
  and and_4 (and_4_out, WE, d4);
  and and_5 (and_5_out, WE, d5);
  and and_6 (and_6_out, WE, d6);
  and and_7 (and_7_out, WE, d7);
  and and_8 (and_8_out, WE, d8);
  and and_9 (and_9_out, WE, d9);
  and and_10 (and_10_out, WE, d10);
  and and_11 (and_11_out, WE, d11);
  and and_12 (and_12_out, WE, d12);
  and and_13 (and_13_out, WE, d13);
  and and_14 (and_14_out, WE, d14);
  and and_15 (and_15_out, WE, d15);
  and and_16 (and_16_out, WE, d16);
  and and_17 (and_17_out, WE, d17);
  and and_18 (and_18_out, WE, d18);
  and and_19 (and_19_out, WE, d19);
  and and_20 (and_20_out, WE, d20);
  and and_21 (and_21_out, WE, d21);
  and and_22 (and_22_out, WE, d22);
  and and_23 (and_23_out, WE, d23);
  and and_24 (and_24_out, WE, d24);
  and and_25 (and_25_out, WE, d25);
  and and_26 (and_26_out, WE, d26);
  and and_27 (and_27_out, WE, d27);
  and and_28 (and_28_out, WE, d28);
  and and_29 (and_29_out, WE, d29);
  and and_30 (and_30_out, WE, d30);
  and and_31 (and_31_out, WE, d31);
  Register #(.width(32)) register_1 (.D(WD), .en(and_1_out), .Q(o1), .clk(Clk), .clr(Reset));
  Register #(.width(32)) register_2 (.D(WD), .en(and_2_out), .Q(o2), .clk(Clk), .clr(Reset));
  Register #(.width(32)) register_3 (.D(WD), .en(and_3_out), .Q(o3), .clk(Clk), .clr(Reset));
  Register #(.width(32)) register_4 (.D(WD), .en(and_4_out), .Q(o4), .clk(Clk), .clr(Reset));
  Register #(.width(32)) register_5 (.D(WD), .en(and_5_out), .Q(o5), .clk(Clk), .clr(Reset));
  Register #(.width(32)) register_6 (.D(WD), .en(and_6_out), .Q(o6), .clk(Clk), .clr(Reset));
  Register #(.width(32)) register_7 (.D(WD), .en(and_7_out), .Q(o7), .clk(Clk), .clr(Reset));
  Register #(.width(32)) register_8 (.D(WD), .en(and_8_out), .Q(o8), .clk(Clk), .clr(Reset));
  Register #(.width(32)) register_9 (.D(WD), .en(and_9_out), .Q(o9), .clk(Clk), .clr(Reset));
  Register #(.width(32)) register_10 (.D(WD), .en(and_10_out), .Q(o10), .clk(Clk), .clr(Reset));
  Register #(.width(32)) register_11 (.D(WD), .en(and_11_out), .Q(o11), .clk(Clk), .clr(Reset));
  Register #(.width(32)) register_12 (.D(WD), .en(and_12_out), .Q(o12), .clk(Clk), .clr(Reset));
  Register #(.width(32)) register_13 (.D(WD), .en(and_13_out), .Q(o13), .clk(Clk), .clr(Reset));
  Register #(.width(32)) register_14 (.D(WD), .en(and_14_out), .Q(o14), .clk(Clk), .clr(Reset));
  Register #(.width(32)) register_15 (.D(WD), .en(and_15_out), .Q(o15), .clk(Clk), .clr(Reset));
  Register #(.width(32)) register_16 (.D(WD), .en(and_16_out), .Q(o16), .clk(Clk), .clr(Reset));
  Register #(.width(32)) register_17 (.D(WD), .en(and_17_out), .Q(o17), .clk(Clk), .clr(Reset));
  Register #(.width(32)) register_18 (.D(WD), .en(and_18_out), .Q(o18), .clk(Clk), .clr(Reset));
  Register #(.width(32)) register_19 (.D(WD), .en(and_19_out), .Q(o19), .clk(Clk), .clr(Reset));
  Register #(.width(32)) register_20 (.D(WD), .en(and_20_out), .Q(o20), .clk(Clk), .clr(Reset));
  Register #(.width(32)) register_21 (.D(WD), .en(and_21_out), .Q(o21), .clk(Clk), .clr(Reset));
  Register #(.width(32)) register_22 (.D(WD), .en(and_22_out), .Q(o22), .clk(Clk), .clr(Reset));
  Register #(.width(32)) register_23 (.D(WD), .en(and_23_out), .Q(o23), .clk(Clk), .clr(Reset));
  Register #(.width(32)) register_24 (.D(WD), .en(and_24_out), .Q(o24), .clk(Clk), .clr(Reset));
  Register #(.width(32)) register_25 (.D(WD), .en(and_25_out), .Q(o25), .clk(Clk), .clr(Reset));
  Register #(.width(32)) register_26 (.D(WD), .en(and_26_out), .Q(o26), .clk(Clk), .clr(Reset));
  Register #(.width(32)) register_27 (.D(WD), .en(and_27_out), .Q(o27), .clk(Clk), .clr(Reset));
  Register #(.width(32)) register_28 (.D(WD), .en(and_28_out), .Q(o28), .clk(Clk), .clr(Reset));
  Register #(.width(32)) register_29 (.D(WD), .en(and_29_out), .Q(o29), .clk(Clk), .clr(Reset));
  Register #(.width(32)) register_30 (.D(WD), .en(and_30_out), .Q(o30), .clk(Clk), .clr(Reset));
  Register #(.width(32)) register_31 (.D(WD), .en(and_31_out), .Q(o31), .clk(Clk), .clr(Reset));
  Multiplexer #(.select(5), .width(32)) multiplexer_1 (
    .in0({32{1'b0}}), .in1(o1), .in2(o2), .in3(o3), .in4(o4), .in5(o5), .in6(o6), .in7(o7), .in8(o8),
    .in9(o9), .in10(o10), .in11(o11), .in12(o12), .in13(o13), .in14(o14), .in15(o15), .in16(o16), .in17(o17),
    .in18(o18), .in19(o19), .in20(o20), .in21(o21), .in22(o22), .in23(o23), .in24(o24), .in25(o25),
    .in26(o26), .in27(o27), .in28(o28), .in29(o29), .in30(o30), .in31(o31), .out(busA), .sel(RA));  // open: en
  Multiplexer #(.select(5), .width(32)) multiplexer_2 (
    .in0({32{1'b0}}), .in1(o1), .in2(o2), .in3(o3), .in4(o4), .in5(o5), .in6(o6), .in7(o7), .in8(o8),
    .in9(o9), .in10(o10), .in11(o11), .in12(o12), .in13(o13), .in14(o14), .in15(o15), .in16(o16), .in17(o17),
    .in18(o18), .in19(o19), .in20(o20), .in21(o21), .in22(o22), .in23(o23), .in24(o24), .in25(o25),
    .in26(o26), .in27(o27), .in28(o28), .in29(o29), .in30(o30), .in31(o31), .out(busB), .sel(RB));  // open: en

  // Other names for the same wires on the sheet: a1[4:0] = RA; a2[4:0] = RB; cl = Clk; d[31:0] = WD; e = WE;
  //   r = Reset
endmodule

module IFU (
  input  Zero,
  input  Br,
  input  [31:0] Imm,
  input  Reset,
  input  Clk,
  output [31:0] Do
);

  wire sel;
  wire [31:0] adder_1_out, adder_2_out, multiplexer_1_out, PC_q;

  and and_1 (sel, Zero, Br);
  Multiplexer #(.width(32)) multiplexer_1 (
    .in0(adder_2_out), .in1(adder_1_out), .out(multiplexer_1_out), .sel(sel));  // open: en
  Adder #(.width(32)) adder_1 (.a(Imm), .b(adder_2_out), .out(adder_1_out));  // open: cin, cout
  Register #(.width(32)) PC (.D(multiplexer_1_out), .Q(PC_q), .clk(Clk), .clr(Reset));  // open: en
  Adder #(.width(32)) adder_2 (.a(PC_q), .b(32'h1), .out(adder_2_out));  // open: cin, cout
  ROM #(.addrWidth(5), .dataWidth(32)) rom_1 (.addr(PC_q[4:0]), .data(Do));  // open: sel

  // Other names for the same wires on the sheet: im[31:0] = Imm; rst = Reset

  // Notes on the sheet:
  //   contents of rom_1 (hex, n*v repeats v):
  //   24*0 3c1021ea 3c0004d3 3c16115b 3c184f06 3c1215de 1000ffff
endmodule

module EXT (
  input  [15:0] Imm16,
  input  ExtOp,
  output [31:0] Imm32
);

  wire [31:0] bit_extender_1_out, bit_extender_2_out;

  assign bit_extender_1_out = {{16{1'b0}}, Imm16};  // Bit_Extender bit_extender_1
  assign bit_extender_2_out = {{16{Imm16[15]}}, Imm16};  // Bit_Extender bit_extender_2
  Multiplexer #(.width(32)) multiplexer_1 (
    .in0(bit_extender_1_out), .in1(bit_extender_2_out), .out(Imm32), .sel(ExtOp));  // open: en
endmodule

module ALU (
  input  [31:0] A,
  input  [31:0] B,
  input  [3:0] ALUCtr,
  output zero,
  output [31:0] Imm32
);

  wire [31:0] add, \and , l16, \or , sub;

  Adder #(.width(32)) adder_1 (.a(A), .b(B), .out(add));  // open: cin, cout
  Subtractor #(.width(32)) subtractor_1 (.a(A), .b(B), .out(sub));  // open: bin, bout
  Shifter #(.width(32)) shifter_1 (.in(B), .\dist (5'b10000), .out(l16));
  assign \and  = A & B;  // AND_Gate and_1, 32 bits wide
  assign \or  = A | B;  // OR_Gate or_1, 32 bits wide
  Multiplexer #(.select(4), .width(32)) multiplexer_1 (
    .in0(add), .in1(sub), .in2(\and ), .in3(\or ), .in4(l16), .out(Imm32), .sel(ALUCtr));  // open: in5, in6, in7, in8, in9, in10, in11, in12, in13, in14, in15, en
  Comparator #(.width(32)) comparator_1 (.a({32{1'b0}}), .b(Imm32), .eq(zero));  // open: gt, lt
endmodule

module DM (
  input  [31:0] Addr,
  input  Reset,
  input  WrEn,
  input  LdEn,
  input  [31:0] DataIn,
  input  Clk,
  output [31:0] MenData
);

  RAM #(.addrWidth(5), .dataWidth(32), .bus("separate")) ram_1 (
    .addr(Addr[6:2]), .din(DataIn), .data(MenData), .str(WrEn), .clk(Clk), .ld(LdEn), .clr(Reset));  // open: sel
endmodule

module Controller (
  input  [5:0] func,
  input  [5:0] OpCode,
  output [3:0] ALUCtr,
  output RegDst,
  output RegWrite,
  output MemtoReg,
  output ALUSrc,
  output MemWrite,
  output nPC_sel,
  output ExtOp
);

  wire addu, beq, lui, lw, nop, not_1_out, not_2_out, not_3_out, not_4_out, not_5_out, not_6_out, not_7_out,
       not_8_out, not_9_out, not_10_out, not_11_out, not_12_out, ori, R, subu, sw;

  not not_1 (not_1_out, OpCode[4]);
  not not_2 (not_2_out, OpCode[5]);
  or or_1 (RegDst, addu, subu);
  not not_3 (not_3_out, OpCode[3]);
  not not_4 (not_4_out, OpCode[2]);
  not not_5 (not_5_out, OpCode[1]);
  not not_6 (not_6_out, OpCode[0]);
  or or_2 (RegWrite, addu, subu, ori, lw, lui);
  or or_3 (ALUSrc, ori, lw, sw, lui);
  and and_1 (R, not_6_out, not_5_out, not_4_out, not_3_out, not_1_out, not_2_out);
  and and_2 (ori, not_2_out, not_1_out, OpCode[3], OpCode[2], not_5_out, OpCode[0]);
  and and_3 (lw, OpCode[5], not_1_out, not_3_out, not_4_out, OpCode[1], OpCode[0]);
  and and_4 (sw, OpCode[5], not_1_out, OpCode[3], not_4_out, OpCode[1], OpCode[0]);
  and and_5 (beq, not_2_out, not_1_out, not_3_out, OpCode[2], not_5_out, not_6_out);
  and and_6 (lui, not_2_out, not_1_out, OpCode[3], OpCode[2], OpCode[1], OpCode[0]);
  buf or_4 (MemtoReg, lw);  // OR_Gate
  buf or_5 (MemWrite, sw);  // OR_Gate
  not not_7 (not_7_out, func[5]);
  buf or_6 (nPC_sel, beq);  // OR_Gate
  not not_8 (not_8_out, func[1]);
  not not_9 (not_9_out, func[3]);
  not not_10 (not_10_out, func[2]);
  not not_11 (not_11_out, func[4]);
  or or_7 (ExtOp, lw, sw, beq);
  not not_12 (not_12_out, func[0]);
  or or_8 (ALUCtr[0], subu, ori, beq);
  and and_7 (addu, func[5], not_11_out, not_9_out, not_10_out, not_8_out, func[0], R);
  and and_8 (subu, func[5], not_11_out, not_9_out, not_10_out, func[1], func[0], R);
  and and_9 (nop, not_7_out, not_11_out, not_9_out, not_10_out, not_8_out, not_12_out, R);
  buf or_9 (ALUCtr[1], ori);  // OR_Gate
  buf or_10 (ALUCtr[2], lui);  // OR_Gate
  buf or_11 (ALUCtr[3], 1'b0);  // OR_Gate

  // Other names for the same wires on the sheet: a0 = ALUCtr[0]; a1 = ALUCtr[1]; a2 = ALUCtr[2]; a3 = ALUCtr[3]
endmodule
